# Fritzing sketch Clock (saved by Fritzing 0.9.3b)

parts:
  U1 = ESP8266 WiFi Module [part_number=ESP8266]
  IC1 = IC, DIP package, 16 pins [chip_label=74595]
  IC2 = IC, DIP package, 16 pins [chip_label=74141]
  S2 = SWITCH-MOMENTARY-2 [package=tactile-switch-1101ne]
  IC4 = Voltage Regulator [part_number=7805 package=78xxl]
  IC3 = V_REG_LD1117VXX [part_number=HT7333 package=78xxl]
  Q1 = PNP-Transistor [part_number=MPSA92 package="TO92 [THT]"]
  Q2 = NPN-Transistor [part_number=MPSA42 package="TO92 [THT]"]
  R2 = Resistor [tolerance=±5% resistance=10k package=THT]
  R3 = Resistor [tolerance=±5% resistance=1M package=THT]
  R4 = Resistor [tolerance=±5% resistance=10k package=THT]
  R5 = Resistor [tolerance=±5% resistance=10k package=THT]
  NIXIE1 = IN-12 Nixie tube [part_number=IN-12]

nets:
  N1: U1.RXD, S2.2
  N2: U1.VCC, IC3.OUT
  GND: U1.GND, IC1.pin8, IC1.pin13, IC2.pin12, S2.1, IC4.GND, IC3.GND, Q2.E
  N3: U1.GPIO_15, IC1.pin14
  N4: U1.GPIO_4, IC1.pin12
  N5: U1.GPIO_5, IC1.pin11
  N6: U1.GPIO_16, IC2.pin3
  N7: U1.GPIO_14, IC2.pin7
  N8: U1.GPIO_12, IC2.pin4
  N9: U1.GPIO_13, IC2.pin6
  N10: IC1.pin10, IC1.pin16, IC2.pin5, IC4.OUT, IC3.IN
  N11: IC1.pin15, R4.Pin_0
  9V: IC4.IN
  180V: Q1.E, R2.Pin_1
  N12: Q1.B, R2.Pin_0, R3.Pin_1
  N13: Q1.C, R5.Pin_0
  N14: Q2.B, R4.Pin_1
  N15: Q2.C, R3.Pin_0
  N16: R5.Pin_1, NIXIE1.Anode

custom parts:
  IN-12 Nixie tube: Russian IN-12 Nixie neon indicator tube
